// Logisim project adder.circ as structural Verilog: 3 circuits, main circuit main
module main (
  input  sub,
  input  [15:0] A,
  input  [15:0] B,
  output ovf,
  output [15:0] result
);

  wire bit0_out, bit1_out, bit2_out, bit3_out, bit4_out, bit5_out, bit6_out, bit7_out, bit8_out, bit9_out,
       bit10_out, bit11_out, bit12_out, bit13_out, bit14_out, bit15_out, xor_1_out, xor_2_out, xor_3_out,
       xor_4_out, xor_5_out, xor_6_out, xor_7_out, xor_8_out, xor_9_out, xor_10_out, xor_11_out, xor_12_out,
       xor_13_out, xor_14_out, xor_15_out, xor_16_out;

  tediadd tediadd_1 ();  // open: a, b, out, in, sum
  tediadd bit15 (.a(xor_1_out), .b(B[15]), .out(bit15_out), .in(bit14_out), .sum(result[15]));
  xor xor_1 (xor_1_out, A[15], sub);
  xor xor_2 (xor_2_out, A[14], sub);
  tediadd bit14 (.a(xor_2_out), .b(B[14]), .out(bit14_out), .in(bit13_out), .sum(result[14]));
  xor xor_3 (xor_3_out, A[13], sub);
  tediadd bit13 (.a(xor_3_out), .b(B[13]), .out(bit13_out), .in(bit12_out), .sum(result[13]));
  xor xor_4 (xor_4_out, A[12], sub);
  tediadd bit12 (.a(xor_4_out), .b(B[12]), .out(bit12_out), .in(bit11_out), .sum(result[12]));
  xor xor_5 (xor_5_out, A[11], sub);
  tediadd bit11 (.a(xor_5_out), .b(B[11]), .out(bit11_out), .in(bit10_out), .sum(result[11]));
  xor xor_6 (xor_6_out, A[10], sub);
  tediadd bit10 (.a(xor_6_out), .b(B[10]), .out(bit10_out), .in(bit9_out), .sum(result[10]));
  tediadd bit9 (.a(xor_7_out), .b(B[9]), .out(bit9_out), .in(bit8_out), .sum(result[9]));
  xor xor_7 (xor_7_out, A[9], sub);
  tediadd bit8 (.a(xor_8_out), .b(B[8]), .out(bit8_out), .in(bit7_out), .sum(result[8]));
  xor xor_8 (xor_8_out, A[8], sub);
  tediadd bit7 (.a(xor_9_out), .b(B[7]), .out(bit7_out), .in(bit6_out), .sum(result[7]));
  xor xor_9 (xor_9_out, A[7], sub);
  xor xor_10 (xor_10_out, A[6], sub);
  tediadd bit6 (.a(xor_10_out), .b(B[6]), .out(bit6_out), .in(bit5_out), .sum(result[6]));
  tediadd bit5 (.a(xor_11_out), .b(B[5]), .out(bit5_out), .in(bit4_out), .sum(result[5]));
  xor xor_11 (xor_11_out, A[5], sub);
  xor xor_12 (xor_12_out, A[4], sub);
  tediadd bit4 (.a(xor_12_out), .b(B[4]), .out(bit4_out), .in(bit3_out), .sum(result[4]));
  tediadd bit3 (.a(xor_13_out), .b(B[3]), .out(bit3_out), .in(bit2_out), .sum(result[3]));
  xor xor_13 (xor_13_out, A[3], sub);
  xor xor_14 (xor_14_out, A[2], sub);
  tediadd bit2 (.a(xor_14_out), .b(B[2]), .out(bit2_out), .in(bit1_out), .sum(result[2]));
  xor xor_15 (xor_15_out, A[1], sub);
  tediadd bit1 (.a(xor_15_out), .b(B[1]), .out(bit1_out), .in(bit0_out), .sum(result[1]));
  xor xor_16 (xor_16_out, A[0], sub);
  tediadd bit0 (.a(xor_16_out), .b(B[0]), .out(bit0_out), .in(sub), .sum(result[0]));
  xor xor_17 (ovf, bit15_out, bit14_out);
endmodule

module tediadd (
  input  a,
  input  b,
  input  in,
  output out,
  output sum
);

  wire and_1_out, and_2_out, xor_1_out;

  and and_1 (and_1_out, b, a);
  xor xor_1 (xor_1_out, a, b);
  or or_1 (out, and_1_out, and_2_out);
  and and_2 (and_2_out, xor_1_out, in);
  xor xor_2 (sum, in, xor_1_out);
endmodule

module threeBitAdd (
  input  [2:0] in_1,
  input  [2:0] in_2,
  input  in_3,
  output [2:0] out_4
);

  wire tediadd_2_out, tediadd_3_out, xor_1_out, xor_2_out, xor_3_out;

  xor xor_1 (xor_1_out, in_3, in_2[1]);
  xor xor_2 (xor_2_out, in_3, in_2[0]);
  tediadd tediadd_1 (.a(in_1[2]), .b(xor_3_out), .in(tediadd_2_out), .sum(out_4[2]));  // open: out
  xor xor_3 (xor_3_out, in_3, in_2[2]);
  tediadd tediadd_2 (.a(xor_1_out), .b(in_1[1]), .out(tediadd_2_out), .in(tediadd_3_out), .sum(out_4[1]));
  tediadd tediadd_3 (.a(in_1[0]), .b(xor_2_out), .out(tediadd_3_out), .in(in_3), .sum(out_4[0]));
endmodule
