// Logisim project fsm.circ as structural Verilog: 1 circuit, main circuit main
module main (
  input  in1,
  input  in2,
  output out
);

  wire anb_out, and_1_out, bnc_out, clock_1_out, D_out, E_out, nabc_out, nanbc_out, none_out, not_1_out,
       nq1nq2_out, Nq1q2_out, nq1q2nq3_out, or_1_out, or_2_out, or_3_out, or_4_out, q1_q, q1_qn,
       q1nq2nq3_out, q2_q, q2_qn, q3_q, q3_qn, xor_1_out;

  xor xor_1 (xor_1_out, in1, in2);
  not not_1 (not_1_out, xor_1_out);
  or or_1 (or_1_out, anb_out, nanbc_out);
  and D (D_out, xor_1_out, or_1_out);
  and E (E_out, not_1_out, bnc_out);
  or or_2 (or_2_out, nanbc_out, bnc_out);
  and and_1 (and_1_out, or_2_out, xor_1_out);
  or or_3 (or_3_out, and_1_out, nabc_out);
  Clock clock_1 (.out(clock_1_out));
  or or_4 (or_4_out, D_out, E_out, none_out);
  D_Flip_Flop q1 (.D(or_3_out), .clk(clock_1_out), .Q(q1_q), .Qn(q1_qn));  // open: preset, reset
  D_Flip_Flop q2 (.D(not_1_out), .clk(clock_1_out), .Q(q2_q), .Qn(q2_qn));  // open: preset, reset
  D_Flip_Flop q3 (.D(or_4_out), .clk(clock_1_out), .Q(q3_q), .Qn(q3_qn));  // open: preset, reset
  and Nq1q2 (Nq1q2_out, q1_qn, q2_q);
  and nabc (nabc_out, Nq1q2_out, q3_q);
  and q1nq2nq3 (q1nq2nq3_out, q1_q, q2_qn, q3_qn);
  and nq1q2nq3 (nq1q2nq3_out, Nq1q2_out, q3_qn);
  and nq1nq2 (nq1nq2_out, q1_qn, q2_qn);
  and bnc (bnc_out, q2_q, q3_qn);
  and nanbc (nanbc_out, nq1nq2_out, q3_q);
  and none (none_out, nq1nq2_out, q3_qn);
  and anb (anb_out, q1_q, q2_qn);
  or or_5 (out, q1nq2nq3_out, nq1q2nq3_out);
endmodule
